# Fritzing sketch Prototype (saved by Fritzing 0.9.3b)

parts:
  Part1 = Adafruit LM3671 Buck Converter [part_number="Adafruit #2745"]
  Part2 = Adafruit 4-channel I2C-safe Bi-directional Logic Level Converter [part_number="Adafruit #757"]
  Part3 = Adafruit LM3671 Buck Converter [part_number="Adafruit #2745"]
  U1 = ESP8266 WiFi Module [part_number=ESP8266]
  J1 = JST-B3P-VH [part_number=JST-B3P-VH package=THT]

nets:
  N1: Part1.EN, Part1.VIN, J1.pin3
  3.3V: Part1.3.3V, Part2.LV, Part3.EN, Part3.VIN, U1.VCC, U1.RST, U1.CH_PD
  GND: Part1.GND, Part2.GND, Part3.GND, U1.GND, J1.pin1
  N2: Part2.A4, J1.pin2
  N3: Part2.B4, U1.GPIO_0
  N4: Part2.HV, Part3.3.3V

custom parts:
  Adafruit LM3671 Buck Converter: Your power supply problems just got SUPER SOLVED! This 3.3V Buck Converter Breakout board is great for supplying power to low voltage circuits from a single Li-Ion cell battery or USB power. This chip provides up to 600-mA load current across the entire input voltage range of 3.5 to 5.5V. Great for your portable project, we made this "pin compatible" with the LM1117-3.3V TO-220 chip so you can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
  Adafruit 4-channel I2C-safe Bi-directional Logic Level Converter: Because the Arduino (and Basic Stamp) are 5V devices, and most modern sensors, displays, flash cards and modes are 3.3V-only, many makers find that they need to perform level shifting/conversion to protect the 3.3V device from 5V. We do have some other handy level shifters in the shop, from the DIP 74LVC245 to the fancy bi-directional TXB0108. However, neither of these are happy to work with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
  ESP8266 WiFi Module: Generic WiFi Module based on the ESP8266 with onboard PCB antenna and UART communications
